# Fritzing sketch RGB-LED-StripLighting (saved by Fritzing 1.0.4)
breadboards: 1

parts:
  R1 = Resistor [tolerance=±5% power=0.25W resistance=1k package=THT]
  R2 = Resistor [tolerance=±5% power=0.25W resistance=1k package=THT]
  Q2 = NPN-Transistor [package="TO92 [THT]"]
  R3 = Resistor [tolerance=±5% power=0.25W resistance=1k package=THT]
  Q3 = NPN-Transistor [package="TO92 [THT]"]
  A1 = ESP32-C6-DevKitC-1
  RGB_Strip_LED1 = RGB Strip LED
  S2 = Pushbutton [package="[THT]"]
  Q1 = NPN-Transistor [package="TO92 [THT]"]

nets:
  N1: R1.Pin_0, A1.Pin_26
  N2: R1.Pin_1, Q1.B
  N3: R2.Pin_0, A1.Pin_25
  N4: R2.Pin_1, Q2.B
  N5: Q2.E, RGB_Strip_LED1.Green_Connect
  N6: Q2.C, Q3.C, A1.Pin_15, A1.Pin_18, A1.Pin_32, S2.Pin_1, S2.Pin_2, Q1.C
  N7: R3.Pin_0, A1.Pin_24
  N8: R3.Pin_1, Q3.B
  N9: Q3.E, RGB_Strip_LED1.Blue_Connect
  N10: A1.Pin_14, RGB_Strip_LED1.Common_Connect
  N11: A1.Pin_23, S2.Pin_3, S2.Pin_4
  N12: RGB_Strip_LED1.Red_Connect, Q1.E

notes:
  Note: Using BC337B NPN, CBE so emitter is on the right, and goes to ground.

custom parts:
  ESP32-C6-DevKitC-1: ESP32-C6-DevKitC-1 is an entry-level development board based on ESP32-C6-WROOM-1(U), a general-purpose module with a 8 MB SPI flash. This board integrates complete Wi-Fi, Bluetooth LE, Zigbee, and Thread functions.
  RGB Strip LED: A tri-color Strip LED with red, green and blue. Based on LED SMD 5050 RGB Pin order: common cathode - green - red - blue
